# Fritzing sketch DiagramaDisplayErgonomia (saved by Fritzing 0.9.3b)

parts:
  MCU1 = Raspberry Pi Zero
  Componente2 = Adafruit ADS1115 16Bit I2C ADC [part_number="Adafruit #1085"]
  J1 = DHT11 basic temperature-humidity sensor [form="♂ (male)" package=THT]
  Componente4 = MQ-7 breakout
  Mic1 = KY-038
  Part1 = ML8511 Breakout Board
  Componente5 = Adafruit TSL2561 [part_number="Adafruit #439"]
  Componente6 = 12 NeoPixel Ring [part_number=1643]

nets:
  VDD: MCU1.pin_1, MCU1.pin_17, Componente2.VDD, Part1.3V3, Componente5.3.3V
  N1: MCU1.pin_3, Componente2.SDA, Componente5.SDA
  N2: MCU1.pin_5, Componente2.SCL, Componente5.SCL
  N3: MCU1.pin_7, J1.OUT
  N4: MCU1.pin_11, Part1.GND
  N5: MCU1.pin_32, Componente6.IN
  N6: Componente2.AIN2, Mic1.pin1
  N7: Componente2.AIN1, Componente4.AO
  N8: Componente2.AIN0, Part1.OUT

notes:
  5V GND
  3.3V GND
  NeoDigitos
  I2C
  chan0
  chan1
  chan2
  GPIO04
  GPIO12

custom parts:
  Adafruit ADS1115 16Bit I2C ADC: For microcontrollers without an analog-to-digital converter or when you want a higher-precision ADC, the ADS1115 provides 16-bit precision at 860 samples/second over I2C. The chip can be configured as 4 single-ended input channels, or two differential channels. As a nice bonus, it even includes a programmable gain amplifier, up to x16, to help boost up smaller single/differential signals to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
  DHT11 basic temperature-humidity sensor: The DHT11 is a basic, ultra low-cost digital temperature and humidity sensor. It uses a capacitive humidity sensor and a thermistor to measure the surrounding air, and spits out a digital signal on the data pin (no analog input pins needed). Its fairly simple to use, but requires careful timing to grab data. The only real downside of this sensor is you can only get new data from it once every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
  MQ-7 breakout: SKU: 101282
  KY-038: ky-038 Microphone sound sensor module
  ML8511 Breakout Board: This breakout board uses the ML8511 UV (ultraviolet) light sensor. The ML8511 works best with light in the 280-390nm wavelengths. The board operates at 2.7 to 3.6V.
  Adafruit TSL2561: The TSL2561 luminosity sensor is an advanced digital light sensor, ideal for use in a wide range of light situations. Compared to low cost CdS cells, this sensor is more precise, allowing for exact lux calculations and can be configured for different gain/timing ranges to detect light ranges from up to 0.1 - 40,000+ Lux on the fly. The best part of this sensor is that it contains both infrared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
  12 NeoPixel Ring: 12 ultra bright smart LED NeoPixels are arranged in a circle with 1.5" (37mm) outer diameter. The rings are 'chainable' - connect the output pin of one to the input pin of another. Use only one microcontroller pin to control as many as you can chain together! Each LED is addressable as the driver chip is inside the LED. Each one has ~18mA constant current drive so the color will be very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
